# Fritzing sketch WifiSesonrTempIR (saved by Fritzing 0.9.3b)
breadboards: 1

parts:
  U1 = NodeMCU V1.0
  R1 = Resistor [tolerance=±5% resistance=220 package="0603 [SMD]"]
  R2 = Resistor [tolerance=±5% resistance=220 package="0603 [SMD]"]
  R3 = Resistor [tolerance=±5% resistance=220 package="0603 [SMD]"]
  DHT1 = DHT11 Humitidy and Temperature Sensor
  LED3 = RGB LED (com. cathode, rgb) [package="5 mm [THT]"]
  SW-1 = Vibration sensor module
  Part1 = Matrix LED de 8x8 basada en MAX7219

nets:
  N1: U1.D1, DHT1.DATA
  N2: U1.D2, R1.Pin_1
  N3: U1.D3, R2.Pin_1
  N4: U1.D4, R3.Pin_1
  VCC: U1.3V3, SW-1.vcc, Part1.VCC
  GND: U1.GND, DHT1.GND, LED3.common_cathode, SW-1.Ground, Part1.GND
  N5: U1.D5, SW-1.Digital_output
  N6: U1.D6, Part1.CLK
  N7: U1.D7, Part1.CS
  N8: U1.D8, Part1.DIN
  VIN: U1.Vin, DHT1.VDD
  N9: R1.Pin_0, LED3.red_anode
  N10: R2.Pin_0, LED3.green_anode
  N11: R3.Pin_0, LED3.blue_anode

custom parts:
  NodeMCU V1.0: ESP8266 based NodeMCU
  DHT11 Humitidy and Temperature Sensor: DHT11 Humidity and Temperature Sensor
  Vibration sensor module: Single-roller type full induction trigger switch. When no vibration or tilt, the product is ON conduction state, and in the steady state, when a vibration or tilt, the switch will be rendered instantly disconnect the conductive resistance increases, generating a current pulse signal, thereby triggering circuit. The default state of the swith is close Digital output Supply voltage:3.3V-5V On-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
